// Logisim project half_adder.circ as structural Verilog: 1 circuit, main circuit main
module main (
  input  A,
  input  A_2,
  input  B,
  input  B_2,
  input  A_3,
  input  A_4,
  input  in_7,
  input  B_3,
  output out_9,
  output out_10,
  output out_11,
  output out_12,
  output out_13,
  output out_14,
  output out_15,
  output out_16
);

  xor xor_1 (out_9, A, B);
  and and_1 (out_11, A, B);
  xor xor_2 (out_13, A_3, in_7);
  and and_2 (out_15, A_3, in_7);
  xor xor_3 (out_14, A_4, B_3);
  and and_3 (out_16, A_4, B_3);
  xor xor_4 (out_10, A_2, B_2);
  and and_4 (out_12, A_2, B_2);

  // Notes on the sheet:
  //   B
  //   HALF_ADDER
endmodule
